# Fritzing sketch scheme (saved by Fritzing 0.9.10b)
breadboards: 1

parts:
  LED1 = LED - 5mm [color="Yellow (595nm)" current=0.030 package="5 mm [THT]"]
  LED2 = LED - 5mm [color="Yellow (595nm)" current=0.030 package="5 mm [THT]"]
  LED3 = LED - 5mm [color="Yellow (595nm)" current=0.030 package="5 mm [THT]"]
  LED4 = LED - 5mm [color="Blue (430nm)" current=0.030 package="5 mm [THT]"]
  LED5 = LED - 5mm [color="Blue (430nm)" current=0.030 package="5 mm [THT]"]
  LED6 = LED - 5mm [color="Blue (430nm)" current=0.030 package="5 mm [THT]"]
  R1 = PHOTOCELL [package=photocell-kit]
  R2 = Resistor [tolerance=±5% resistance=220 package="1206 [SMD]"]
  R3 = Resistor [tolerance=±5% resistance=220 package="1206 [SMD]"]
  R4 = Resistor [tolerance=±5% resistance=220 package="1206 [SMD]"]
  Part1 = Soil Moisture Sensor

nets:
  N1: LED1.cathode, LED2.cathode, LED3.cathode, LED4.cathode, LED5.cathode, LED6.cathode, R4.Pin_1, Part1.VCC
  N2: LED1.anode, LED2.anode, LED3.anode, R2.Pin_0
  N3: LED4.anode, LED5.anode, LED6.anode, R3.Pin_1
  N4: R1.P$1, R4.Pin_0
  N5: R1.P$2, Part1.GND

notes:
  ARD_D8
  ARD_A1
  ARD_D7
  GND
  Vcc
  ARD_D4
